# Fritzing sketch ArduinoMIDIController (saved by Fritzing 0.9.3b)
breadboards: 1

parts:
  Part1 = Arduino Uno (Rev3)
  R1 = Rotary Potentiometer (Small) [maximum_resistance=20kΩ package=THT]
  S2 = Pushbutton [package="[THT]"]
  S1 = Pushbutton [package="[SMD]"]
  R2 = Rotary Potentiometer (Small) [maximum_resistance=20kΩ package=THT]
  BUTTON = Pushbutton [package="[THT]"]

nets:
  N1: Part1.A0, R1.wiper
  N2: Part1.A1, R2.wiper
  N3: Part1.D8, S1.Pin_3, S1.Pin_4
  N4: Part1.D9_PWM, S2.Pin_3, S2.Pin_4
  N5: Part1.D10_PWM/SS, BUTTON.Pin_3, BUTTON.Pin_4
  N6: Part1.5V, R1.leg1, R2.leg1
  N7: Part1.GND, R1.leg2, S2.Pin_1, S2.Pin_2, S1.Pin_1, S1.Pin_2, R2.leg2, BUTTON.Pin_1, BUTTON.Pin_2
